// Logisim project CS1409_U201414803_许荣仁_mipscpu.circ as structural Verilog
module decoder1 (
  input  o0,
  input  o1,
  input  o2,
  input  o3,
  input  o4,
  input  o5,
  input  f0,
  input  f1,
  input  f2,
  input  f3,
  input  f4,
  input  f5,
  output add,
  output addi,
  output addiu,
  output addu,
  output \and ,
  output andi,
  output sll,
  output sra,
  output srl,
  output sub,
  output \or ,
  output ori
);

  wire not_1_out, not_2_out, not_3_out, not_4_out, not_5_out, not_6_out, not_7_out, not_8_out, not_9_out,
       not_10_out, not_11_out, not_12_out, not_13_out, not_14_out, not_15_out, not_16_out, not_17_out,
       not_18_out, not_19_out, not_20_out, not_21_out, not_22_out, not_23_out, not_24_out, not_25_out,
       not_26_out, not_27_out, not_28_out, not_29_out, not_30_out, not_31_out, not_32_out, not_33_out,
       not_34_out, not_35_out, not_36_out, not_37_out, not_38_out, not_39_out, not_40_out, not_41_out,
       not_42_out, not_43_out, not_44_out, not_45_out, not_46_out, not_47_out, not_48_out, not_49_out,
       not_50_out, not_51_out, not_52_out, not_53_out, not_54_out, not_55_out, not_56_out, not_57_out,
       not_58_out, not_59_out, not_60_out, not_61_out, not_62_out, not_63_out, not_64_out, not_65_out,
       not_66_out, not_67_out, not_68_out, not_69_out, not_70_out, not_71_out, not_72_out, not_73_out,
       not_74_out, not_75_out, not_76_out, not_77_out, not_78_out, not_79_out, not_80_out, not_81_out,
       not_82_out, not_83_out, not_84_out, not_85_out, not_86_out, not_87_out, not_88_out, not_89_out,
       not_90_out, not_91_out, not_92_out, not_93_out, not_94_out, not_95_out, not_96_out, not_97_out,
       not_98_out, not_99_out;

  not not_1 (not_1_out, o0);
  not not_2 (not_2_out, o1);
  not not_3 (not_3_out, o2);
  not not_4 (not_4_out, o3);
  not not_5 (not_5_out, o4);
  not not_6 (not_6_out, o5);
  not not_7 (not_7_out, f1);
  not not_8 (not_8_out, f2);
  not not_9 (not_9_out, f3);
  not not_10 (not_10_out, f4);
  not not_11 (not_11_out, f5);
  not not_12 (not_12_out, o0);
  not not_13 (not_13_out, o1);
  not not_14 (not_14_out, o3);
  not not_15 (not_15_out, o4);
  not not_16 (not_16_out, o5);
  not not_17 (not_17_out, o0);
  not not_18 (not_18_out, o1);
  not not_19 (not_19_out, o3);
  not not_20 (not_20_out, o4);
  not not_21 (not_21_out, o0);
  not not_22 (not_22_out, o1);
  not not_23 (not_23_out, o2);
  not not_24 (not_24_out, o3);
  not not_25 (not_25_out, o4);
  not not_26 (not_26_out, o5);
  not not_27 (not_27_out, f1);
  not not_28 (not_28_out, f2);
  not not_29 (not_29_out, f3);
  not not_30 (not_30_out, f4);
  not not_31 (not_31_out, o0);
  not not_32 (not_32_out, o1);
  not not_33 (not_33_out, o2);
  not not_34 (not_34_out, o3);
  not not_35 (not_35_out, o4);
  not not_36 (not_36_out, o5);
  not not_37 (not_37_out, f1);
  not not_38 (not_38_out, f2);
  not not_39 (not_39_out, f4);
  not not_40 (not_40_out, f5);
  not not_41 (not_41_out, o0);
  not not_42 (not_42_out, o1);
  not not_43 (not_43_out, o4);
  not not_44 (not_44_out, o5);
  not not_45 (not_45_out, o0);
  not not_46 (not_46_out, o1);
  not not_47 (not_47_out, o2);
  not not_48 (not_48_out, o3);
  not not_49 (not_49_out, o4);
  not not_50 (not_50_out, o5);
  not not_51 (not_51_out, f0);
  not not_52 (not_52_out, f1);
  not not_53 (not_53_out, f2);
  not not_54 (not_54_out, f3);
  not not_55 (not_55_out, f4);
  not not_56 (not_56_out, f5);
  not not_57 (not_57_out, o0);
  not not_58 (not_58_out, o1);
  not not_59 (not_59_out, o2);
  not not_60 (not_60_out, o3);
  not not_61 (not_61_out, o4);
  not not_62 (not_62_out, o5);
  not not_63 (not_63_out, f0);
  not not_64 (not_64_out, f1);
  not not_65 (not_65_out, f2);
  not not_66 (not_66_out, f3);
  not not_67 (not_67_out, o0);
  not not_68 (not_68_out, o1);
  not not_69 (not_69_out, o2);
  not not_70 (not_70_out, o3);
  not not_71 (not_71_out, o4);
  not not_72 (not_72_out, o5);
  not not_73 (not_73_out, f0);
  not not_74 (not_74_out, f1);
  not not_75 (not_75_out, f2);
  not not_76 (not_76_out, f3);
  not not_77 (not_77_out, f5);
  not not_78 (not_78_out, o0);
  not not_79 (not_79_out, o1);
  not not_80 (not_80_out, o2);
  not not_81 (not_81_out, o3);
  not not_82 (not_82_out, o4);
  not not_83 (not_83_out, o5);
  not not_84 (not_84_out, f1);
  not not_85 (not_85_out, f2);
  not not_86 (not_86_out, f3);
  not not_87 (not_87_out, f5);
  not not_88 (not_88_out, o0);
  not not_89 (not_89_out, o1);
  not not_90 (not_90_out, o2);
  not not_91 (not_91_out, o3);
  not not_92 (not_92_out, o4);
  not not_93 (not_93_out, o5);
  not not_94 (not_94_out, f1);
  not not_95 (not_95_out, f2);
  not not_96 (not_96_out, f4);
  not not_97 (not_97_out, o0);
  not not_98 (not_98_out, o1);
  not not_99 (not_99_out, o4);
  and and_1 (add, not_1_out, not_2_out, not_3_out, not_4_out, not_5_out, not_6_out, f0, not_7_out, not_8_out, not_9_out, not_10_out, not_11_out);
  and and_2 (addi, not_12_out, not_13_out, o2, not_14_out, not_15_out, not_16_out);
  and and_3 (addiu, not_17_out, not_18_out, o2, not_19_out, not_20_out, o5);
  and and_4 (addu, not_21_out, not_22_out, not_23_out, not_24_out, not_25_out, not_26_out, f0, not_27_out, not_28_out, not_29_out, not_30_out, f5);
  and and_5 (\and , not_31_out, not_32_out, not_33_out, not_34_out, not_35_out, not_36_out, f0, not_37_out, not_38_out, f3, not_39_out, not_40_out);
  and and_6 (andi, not_41_out, not_42_out, o2, o3, not_43_out, not_44_out);
  and and_7 (sll, not_45_out, not_46_out, not_47_out, not_48_out, not_49_out, not_50_out, not_51_out, not_52_out, not_53_out, not_54_out, not_55_out, not_56_out);
  and and_8 (sra, not_57_out, not_58_out, not_59_out, not_60_out, not_61_out, not_62_out, not_63_out, not_64_out, not_65_out, not_66_out, f4, f5);
  and and_9 (srl, not_67_out, not_68_out, not_69_out, not_70_out, not_71_out, not_72_out, not_73_out, not_74_out, not_75_out, not_76_out, f4, not_77_out);
  and and_10 (sub, not_78_out, not_79_out, not_80_out, not_81_out, not_82_out, not_83_out, f0, not_84_out, not_85_out, not_86_out, f4, not_87_out);
  and and_11 (\or , not_88_out, not_89_out, not_90_out, not_91_out, not_92_out, not_93_out, f0, not_94_out, not_95_out, f3, not_96_out, f5);
  and and_12 (ori, not_97_out, not_98_out, o2, o3, not_99_out, o5);
endmodule

module decoder2 (
  input  o0,
  input  o1,
  input  o2,
  input  o3,
  input  o4,
  input  o5,
  input  f0,
  input  f1,
  input  f2,
  input  f3,
  input  f4,
  input  f5,
  output \nor ,
  output lw,
  output sw,
  output beq,
  output bne,
  output slt,
  output slti,
  output sltu,
  output jump,
  output jmpl,
  output jmpr,
  output syscall
);

  wire not_1_out, not_2_out, not_3_out, not_4_out, not_5_out, not_6_out, not_7_out, not_8_out, not_9_out,
       not_10_out, not_11_out, not_12_out, not_13_out, not_14_out, not_15_out, not_16_out, not_17_out,
       not_18_out, not_19_out, not_20_out, not_21_out, not_22_out, not_23_out, not_24_out, not_25_out,
       not_26_out, not_27_out, not_28_out, not_29_out, not_30_out, not_31_out, not_32_out, not_33_out,
       not_34_out, not_35_out, not_36_out, not_37_out, not_38_out, not_39_out, not_40_out, not_41_out,
       not_42_out, not_43_out, not_44_out, not_45_out, not_46_out, not_47_out, not_48_out, not_49_out,
       not_50_out, not_51_out, not_52_out, not_53_out, not_54_out, not_55_out, not_56_out, not_57_out,
       not_58_out, not_59_out, not_60_out, not_61_out, not_62_out, not_63_out, not_64_out, not_65_out,
       not_66_out, not_67_out, not_68_out, not_69_out, not_70_out, not_71_out, not_72_out, not_73_out;

  not not_1 (not_1_out, o0);
  not not_2 (not_2_out, o1);
  not not_3 (not_3_out, o2);
  not not_4 (not_4_out, o3);
  not not_5 (not_5_out, o4);
  not not_6 (not_6_out, o5);
  not not_7 (not_7_out, f1);
  not not_8 (not_8_out, f2);
  not not_9 (not_9_out, o1);
  not not_10 (not_10_out, o2);
  not not_11 (not_11_out, o3);
  not not_12 (not_12_out, o1);
  not not_13 (not_13_out, o3);
  not not_14 (not_14_out, o0);
  not not_15 (not_15_out, o1);
  not not_16 (not_16_out, o2);
  not not_17 (not_17_out, o4);
  not not_18 (not_18_out, o5);
  not not_19 (not_19_out, o0);
  not not_20 (not_20_out, o1);
  not not_21 (not_21_out, o2);
  not not_22 (not_22_out, o4);
  not not_23 (not_23_out, o0);
  not not_24 (not_24_out, o1);
  not not_25 (not_25_out, o2);
  not not_26 (not_26_out, o3);
  not not_27 (not_27_out, o4);
  not not_28 (not_28_out, o5);
  not not_29 (not_29_out, f1);
  not not_30 (not_30_out, f3);
  not not_31 (not_31_out, f5);
  not not_32 (not_32_out, o0);
  not not_33 (not_33_out, o1);
  not not_34 (not_34_out, o3);
  not not_35 (not_35_out, o5);
  not not_36 (not_36_out, o0);
  not not_37 (not_37_out, o1);
  not not_38 (not_38_out, o2);
  not not_39 (not_39_out, o3);
  not not_40 (not_40_out, o4);
  not not_41 (not_41_out, o5);
  not not_42 (not_42_out, f1);
  not not_43 (not_43_out, f3);
  not not_44 (not_44_out, o0);
  not not_45 (not_45_out, o1);
  not not_46 (not_46_out, o2);
  not not_47 (not_47_out, o3);
  not not_48 (not_48_out, o5);
  not not_49 (not_49_out, o0);
  not not_50 (not_50_out, o1);
  not not_51 (not_51_out, o2);
  not not_52 (not_52_out, o3);
  not not_53 (not_53_out, o0);
  not not_54 (not_54_out, o1);
  not not_55 (not_55_out, o2);
  not not_56 (not_56_out, o3);
  not not_57 (not_57_out, o4);
  not not_58 (not_58_out, o5);
  not not_59 (not_59_out, f0);
  not not_60 (not_60_out, f1);
  not not_61 (not_61_out, f3);
  not not_62 (not_62_out, f4);
  not not_63 (not_63_out, f5);
  not not_64 (not_64_out, o0);
  not not_65 (not_65_out, o1);
  not not_66 (not_66_out, o2);
  not not_67 (not_67_out, o3);
  not not_68 (not_68_out, o4);
  not not_69 (not_69_out, o5);
  not not_70 (not_70_out, f0);
  not not_71 (not_71_out, f1);
  not not_72 (not_72_out, f4);
  not not_73 (not_73_out, f5);
  and and_1 (\nor , not_1_out, not_2_out, not_3_out, not_4_out, not_5_out, not_6_out, f0, not_7_out, not_8_out, f3, f4, f5);
  and and_2 (lw, o0, not_9_out, not_10_out, not_11_out, o4, o5);
  and and_3 (sw, o0, not_12_out, o2, not_13_out, o4, o5);
  and and_4 (beq, not_14_out, not_15_out, not_16_out, o3, not_17_out, not_18_out);
  and and_5 (bne, not_19_out, not_20_out, not_21_out, o3, not_22_out, o5);
  and and_6 (slt, not_23_out, not_24_out, not_25_out, not_26_out, not_27_out, not_28_out, f0, not_29_out, f2, not_30_out, f4, not_31_out);
  and and_7 (slti, not_32_out, not_33_out, o2, not_34_out, o4, not_35_out);
  and and_8 (sltu, not_36_out, not_37_out, not_38_out, not_39_out, not_40_out, not_41_out, f0, not_42_out, f2, not_43_out, f4, f5);
  and and_9 (jump, not_44_out, not_45_out, not_46_out, not_47_out, o4, not_48_out);
  and and_10 (jmpl, not_49_out, not_50_out, not_51_out, not_52_out, o4, o5);
  and and_11 (jmpr, not_53_out, not_54_out, not_55_out, not_56_out, not_57_out, not_58_out, not_59_out, not_60_out, f2, not_61_out, not_62_out, not_63_out);
  and and_12 (syscall, not_64_out, not_65_out, not_66_out, not_67_out, not_68_out, not_69_out, not_70_out, not_71_out, f2, f3, not_72_out, not_73_out);
endmodule

module decoderrr (
  input  o0,
  input  o1,
  input  o2,
  input  o3,
  input  o4,
  input  o5,
  input  f0,
  input  f1,
  input  f2,
  input  f3,
  input  f4,
  input  f5,
  output add,
  output \nor ,
  output lw,
  output addi,
  output sw,
  output addiu,
  output beq,
  output bne,
  output addu,
  output slt,
  output \and ,
  output slti,
  output andi,
  output sltu,
  output sll,
  output jump,
  output jmpl,
  output sra,
  output jmpr,
  output srl,
  output syscall,
  output sub,
  output \or ,
  output ori
);

  wire not_1_out, not_2_out, not_3_out, not_4_out, not_5_out, not_6_out, not_7_out, not_8_out, not_9_out,
       not_10_out, not_11_out, not_12_out, not_13_out, not_14_out, not_15_out, not_16_out, not_17_out,
       not_18_out, not_19_out, not_20_out, not_21_out, not_22_out, not_23_out, not_24_out, not_25_out,
       not_26_out, not_27_out, not_28_out, not_29_out, not_30_out, not_31_out, not_32_out, not_33_out,
       not_34_out, not_35_out, not_36_out, not_37_out, not_38_out, not_39_out, not_40_out, not_41_out,
       not_42_out, not_43_out, not_44_out, not_45_out, not_46_out, not_47_out, not_48_out, not_49_out,
       not_50_out, not_51_out, not_52_out, not_53_out, not_54_out, not_55_out, not_56_out, not_57_out,
       not_58_out, not_59_out, not_60_out, not_61_out, not_62_out, not_63_out, not_64_out, not_65_out,
       not_66_out, not_67_out, not_68_out, not_69_out, not_70_out, not_71_out, not_72_out, not_73_out,
       not_74_out, not_75_out, not_76_out, not_77_out, not_78_out, not_79_out, not_80_out, not_81_out,
       not_82_out, not_83_out, not_84_out, not_85_out, not_86_out, not_87_out, not_88_out, not_89_out,
       not_90_out, not_91_out, not_92_out, not_93_out, not_94_out, not_95_out, not_96_out, not_97_out,
       not_98_out, not_99_out, not_100_out, not_101_out, not_102_out, not_103_out, not_104_out, not_105_out,
       not_106_out, not_107_out, not_108_out, not_109_out, not_110_out, not_111_out, not_112_out,
       not_113_out, not_114_out, not_115_out, not_116_out, not_117_out, not_118_out, not_119_out,
       not_120_out, not_121_out, not_122_out, not_123_out, not_124_out, not_125_out, not_126_out,
       not_127_out, not_128_out, not_129_out, not_130_out, not_131_out, not_132_out, not_133_out,
       not_134_out, not_135_out, not_136_out, not_137_out, not_138_out, not_139_out, not_140_out,
       not_141_out, not_142_out, not_143_out, not_144_out, not_145_out, not_146_out, not_147_out,
       not_148_out, not_149_out, not_150_out, not_151_out, not_152_out, not_153_out, not_154_out,
       not_155_out, not_156_out, not_157_out, not_158_out, not_159_out, not_160_out, not_161_out,
       not_162_out, not_163_out, not_164_out, not_165_out, not_166_out, not_167_out, not_168_out,
       not_169_out, not_170_out, not_171_out, not_172_out;

  not not_1 (not_1_out, o0);
  not not_2 (not_2_out, o1);
  not not_3 (not_3_out, o2);
  not not_4 (not_4_out, o3);
  not not_5 (not_5_out, o4);
  not not_6 (not_6_out, o5);
  not not_7 (not_7_out, f1);
  not not_8 (not_8_out, f2);
  not not_9 (not_9_out, f3);
  not not_10 (not_10_out, f4);
  not not_11 (not_11_out, f5);
  not not_12 (not_12_out, o0);
  not not_13 (not_13_out, o1);
  not not_14 (not_14_out, o3);
  not not_15 (not_15_out, o4);
  not not_16 (not_16_out, o5);
  not not_17 (not_17_out, o0);
  not not_18 (not_18_out, o1);
  not not_19 (not_19_out, o3);
  not not_20 (not_20_out, o4);
  not not_21 (not_21_out, o0);
  not not_22 (not_22_out, o1);
  not not_23 (not_23_out, o2);
  not not_24 (not_24_out, o3);
  not not_25 (not_25_out, o4);
  not not_26 (not_26_out, o5);
  not not_27 (not_27_out, f1);
  not not_28 (not_28_out, f2);
  not not_29 (not_29_out, f3);
  not not_30 (not_30_out, f4);
  not not_31 (not_31_out, o0);
  not not_32 (not_32_out, o1);
  not not_33 (not_33_out, o2);
  not not_34 (not_34_out, o3);
  not not_35 (not_35_out, o4);
  not not_36 (not_36_out, o5);
  not not_37 (not_37_out, f1);
  not not_38 (not_38_out, f2);
  not not_39 (not_39_out, f4);
  not not_40 (not_40_out, f5);
  not not_41 (not_41_out, o0);
  not not_42 (not_42_out, o1);
  not not_43 (not_43_out, o4);
  not not_44 (not_44_out, o5);
  not not_45 (not_45_out, o0);
  not not_46 (not_46_out, o1);
  not not_47 (not_47_out, o2);
  not not_48 (not_48_out, o3);
  not not_49 (not_49_out, o4);
  not not_50 (not_50_out, o5);
  not not_51 (not_51_out, f0);
  not not_52 (not_52_out, f1);
  not not_53 (not_53_out, f2);
  not not_54 (not_54_out, f3);
  not not_55 (not_55_out, f4);
  not not_56 (not_56_out, f5);
  not not_57 (not_57_out, o0);
  not not_58 (not_58_out, o1);
  not not_59 (not_59_out, o2);
  not not_60 (not_60_out, o3);
  not not_61 (not_61_out, o4);
  not not_62 (not_62_out, o5);
  not not_63 (not_63_out, f0);
  not not_64 (not_64_out, f1);
  not not_65 (not_65_out, f2);
  not not_66 (not_66_out, f3);
  not not_67 (not_67_out, o0);
  not not_68 (not_68_out, o1);
  not not_69 (not_69_out, o2);
  not not_70 (not_70_out, o3);
  not not_71 (not_71_out, o4);
  not not_72 (not_72_out, o5);
  not not_73 (not_73_out, f0);
  not not_74 (not_74_out, f1);
  not not_75 (not_75_out, f2);
  not not_76 (not_76_out, f3);
  not not_77 (not_77_out, f5);
  not not_78 (not_78_out, o0);
  not not_79 (not_79_out, o1);
  not not_80 (not_80_out, o2);
  not not_81 (not_81_out, o3);
  not not_82 (not_82_out, o4);
  not not_83 (not_83_out, o5);
  not not_84 (not_84_out, f1);
  not not_85 (not_85_out, f2);
  not not_86 (not_86_out, f3);
  not not_87 (not_87_out, f5);
  not not_88 (not_88_out, o0);
  not not_89 (not_89_out, o1);
  not not_90 (not_90_out, o2);
  not not_91 (not_91_out, o3);
  not not_92 (not_92_out, o4);
  not not_93 (not_93_out, o5);
  not not_94 (not_94_out, f1);
  not not_95 (not_95_out, f2);
  not not_96 (not_96_out, f4);
  not not_97 (not_97_out, o0);
  not not_98 (not_98_out, o1);
  not not_99 (not_99_out, o4);
  and and_1 (addi, not_12_out, not_13_out, o2, not_14_out, not_15_out, not_16_out);
  and and_2 (addiu, not_17_out, not_18_out, o2, not_19_out, not_20_out, o5);
  and and_3 (andi, not_41_out, not_42_out, o2, o3, not_43_out, not_44_out);
  and and_4 (ori, not_97_out, not_98_out, o2, o3, not_99_out, o5);
  and and_5 (add, not_1_out, not_2_out, not_3_out, not_4_out, not_5_out, not_6_out, f0, not_7_out, not_8_out, not_9_out, not_10_out, not_11_out);
  and and_6 (addu, not_21_out, not_22_out, not_23_out, not_24_out, not_25_out, not_26_out, f0, not_27_out, not_28_out, not_29_out, not_30_out, f5);
  and and_7 (\and , not_31_out, not_32_out, not_33_out, not_34_out, not_35_out, not_36_out, f0, not_37_out, not_38_out, f3, not_39_out, not_40_out);
  and and_8 (sll, not_45_out, not_46_out, not_47_out, not_48_out, not_49_out, not_50_out, not_51_out, not_52_out, not_53_out, not_54_out, not_55_out, not_56_out);
  and and_9 (sra, not_57_out, not_58_out, not_59_out, not_60_out, not_61_out, not_62_out, not_63_out, not_64_out, not_65_out, not_66_out, f4, f5);
  and and_10 (srl, not_67_out, not_68_out, not_69_out, not_70_out, not_71_out, not_72_out, not_73_out, not_74_out, not_75_out, not_76_out, f4, not_77_out);
  and and_11 (sub, not_78_out, not_79_out, not_80_out, not_81_out, not_82_out, not_83_out, f0, not_84_out, not_85_out, not_86_out, f4, not_87_out);
  and and_12 (\or , not_88_out, not_89_out, not_90_out, not_91_out, not_92_out, not_93_out, f0, not_94_out, not_95_out, f3, not_96_out, f5);
  not not_100 (not_100_out, o0);
  not not_101 (not_101_out, o1);
  not not_102 (not_102_out, o2);
  not not_103 (not_103_out, o3);
  not not_104 (not_104_out, o4);
  not not_105 (not_105_out, o5);
  not not_106 (not_106_out, f1);
  not not_107 (not_107_out, f2);
  not not_108 (not_108_out, o1);
  not not_109 (not_109_out, o2);
  not not_110 (not_110_out, o3);
  not not_111 (not_111_out, o1);
  not not_112 (not_112_out, o3);
  not not_113 (not_113_out, o0);
  not not_114 (not_114_out, o1);
  not not_115 (not_115_out, o2);
  not not_116 (not_116_out, o4);
  not not_117 (not_117_out, o5);
  not not_118 (not_118_out, o0);
  not not_119 (not_119_out, o1);
  not not_120 (not_120_out, o2);
  not not_121 (not_121_out, o4);
  not not_122 (not_122_out, o0);
  not not_123 (not_123_out, o1);
  not not_124 (not_124_out, o2);
  not not_125 (not_125_out, o3);
  not not_126 (not_126_out, o4);
  not not_127 (not_127_out, o5);
  not not_128 (not_128_out, f1);
  not not_129 (not_129_out, f3);
  not not_130 (not_130_out, f5);
  not not_131 (not_131_out, o0);
  not not_132 (not_132_out, o1);
  not not_133 (not_133_out, o3);
  not not_134 (not_134_out, o5);
  not not_135 (not_135_out, o0);
  not not_136 (not_136_out, o1);
  not not_137 (not_137_out, o2);
  not not_138 (not_138_out, o3);
  not not_139 (not_139_out, o4);
  not not_140 (not_140_out, o5);
  not not_141 (not_141_out, f1);
  not not_142 (not_142_out, f3);
  not not_143 (not_143_out, o0);
  not not_144 (not_144_out, o1);
  not not_145 (not_145_out, o2);
  not not_146 (not_146_out, o3);
  not not_147 (not_147_out, o5);
  not not_148 (not_148_out, o0);
  not not_149 (not_149_out, o1);
  not not_150 (not_150_out, o2);
  not not_151 (not_151_out, o3);
  not not_152 (not_152_out, o0);
  not not_153 (not_153_out, o1);
  not not_154 (not_154_out, o2);
  not not_155 (not_155_out, o3);
  not not_156 (not_156_out, o4);
  not not_157 (not_157_out, o5);
  not not_158 (not_158_out, f0);
  not not_159 (not_159_out, f1);
  not not_160 (not_160_out, f3);
  not not_161 (not_161_out, f4);
  not not_162 (not_162_out, f5);
  not not_163 (not_163_out, o0);
  not not_164 (not_164_out, o1);
  not not_165 (not_165_out, o2);
  not not_166 (not_166_out, o3);
  not not_167 (not_167_out, o4);
  not not_168 (not_168_out, o5);
  not not_169 (not_169_out, f0);
  not not_170 (not_170_out, f1);
  not not_171 (not_171_out, f4);
  not not_172 (not_172_out, f5);
  and and_13 (\nor , not_100_out, not_101_out, not_102_out, not_103_out, not_104_out, not_105_out, f0, not_106_out, not_107_out, f3, f4, f5);
  and and_14 (lw, o0, not_108_out, not_109_out, not_110_out, o4, o5);
  and and_15 (sw, o0, not_111_out, o2, not_112_out, o4, o5);
  and and_16 (beq, not_113_out, not_114_out, not_115_out, o3, not_116_out, not_117_out);
  and and_17 (bne, not_118_out, not_119_out, not_120_out, o3, not_121_out, o5);
  and and_18 (slt, not_122_out, not_123_out, not_124_out, not_125_out, not_126_out, not_127_out, f0, not_128_out, f2, not_129_out, f4, not_130_out);
  and and_19 (slti, not_131_out, not_132_out, o2, not_133_out, o4, not_134_out);
  and and_20 (sltu, not_135_out, not_136_out, not_137_out, not_138_out, not_139_out, not_140_out, f0, not_141_out, f2, not_142_out, f4, f5);
  and and_21 (jump, not_143_out, not_144_out, not_145_out, not_146_out, o4, not_147_out);
  and and_22 (jmpl, not_148_out, not_149_out, not_150_out, not_151_out, o4, o5);
  and and_23 (jmpr, not_152_out, not_153_out, not_154_out, not_155_out, not_156_out, not_157_out, not_158_out, not_159_out, f2, not_160_out, not_161_out, not_162_out);
  and and_24 (syscall, not_163_out, not_164_out, not_165_out, not_166_out, not_167_out, not_168_out, not_169_out, not_170_out, f2, f3, not_171_out, not_172_out);
endmodule

module ctl_unity (
  input  [5:0] o0_no5,
  input  [5:0] f0_nf5,
  output beq,
  output bne,
  output j,
  output jal,
  output jr,
  output alu_src,
  output reg_dst,
  output reg_write,
  output mem_write,
  output memyoReg,
  output ext_u,
  output s_i,
  output [3:0] out_15
);

  wire decoderrr_1_add, decoderrr_1_addi, decoderrr_1_addu, decoderrr_1_and, decoderrr_1_andi,
       decoderrr_1_nor, decoderrr_1_or, decoderrr_1_ori, decoderrr_1_sll, decoderrr_1_slt, decoderrr_1_slti,
       decoderrr_1_sltu, decoderrr_1_sra, decoderrr_1_srl, decoderrr_1_sub, decoderrr_1_syscall;

  decoderrr decoderrr_1 (
    .o0(o0_no5[0]), .o1(o0_no5[1]), .o2(o0_no5[2]), .o3(o0_no5[3]), .o4(o0_no5[4]), .o5(o0_no5[5]),
    .f0(f0_nf5[0]), .f1(f0_nf5[1]), .f2(f0_nf5[2]), .f3(f0_nf5[3]), .f4(f0_nf5[4]), .f5(f0_nf5[5]),
    .add(decoderrr_1_add), .\nor (decoderrr_1_nor), .lw(memyoReg), .addi(decoderrr_1_addi), .sw(mem_write),
    .addiu(ext_u), .beq(beq), .bne(bne), .addu(decoderrr_1_addu), .slt(decoderrr_1_slt),
    .\and (decoderrr_1_and), .slti(decoderrr_1_slti), .andi(decoderrr_1_andi), .sltu(decoderrr_1_sltu),
    .sll(decoderrr_1_sll), .jump(j), .jmpl(jal), .sra(decoderrr_1_sra), .jmpr(jr), .srl(decoderrr_1_srl),
    .syscall(decoderrr_1_syscall), .sub(decoderrr_1_sub), .\or (decoderrr_1_or), .ori(decoderrr_1_ori));
  or op3 (out_15[3], decoderrr_1_nor, decoderrr_1_slt, decoderrr_1_slti, decoderrr_1_sltu, decoderrr_1_or, decoderrr_1_ori);
  or op2 (out_15[2], decoderrr_1_add, memyoReg, decoderrr_1_addi, mem_write, ext_u, decoderrr_1_addu, decoderrr_1_and, decoderrr_1_andi, decoderrr_1_sltu, decoderrr_1_sub);
  or op1 (out_15[1], decoderrr_1_nor, decoderrr_1_slt, decoderrr_1_and, decoderrr_1_slti, decoderrr_1_andi, decoderrr_1_srl, decoderrr_1_sub);
  or op0 (out_15[0], decoderrr_1_add, memyoReg, decoderrr_1_addi, mem_write, ext_u, decoderrr_1_addu, decoderrr_1_slt, decoderrr_1_and, decoderrr_1_slti, decoderrr_1_andi, decoderrr_1_sra);
  or u_alu_src (alu_src, ext_u, decoderrr_1_sll, decoderrr_1_srl, memyoReg, decoderrr_1_addi, mem_write, decoderrr_1_slti, decoderrr_1_andi, decoderrr_1_sra, decoderrr_1_ori);
  or \u_移位立即数  (s_i, decoderrr_1_srl, decoderrr_1_sra, decoderrr_1_sll);
  or u_reg_dst (reg_dst, decoderrr_1_addu, decoderrr_1_or, decoderrr_1_sub, decoderrr_1_srl, decoderrr_1_add, decoderrr_1_nor, decoderrr_1_slt, decoderrr_1_and, decoderrr_1_sltu, decoderrr_1_sll, decoderrr_1_sra, jr);
  or u_reg_write (reg_write, memyoReg, decoderrr_1_srl, decoderrr_1_sra, decoderrr_1_sll, decoderrr_1_sltu, decoderrr_1_andi, decoderrr_1_slti, decoderrr_1_add, decoderrr_1_nor, decoderrr_1_addi, ext_u, decoderrr_1_addu, decoderrr_1_slt, decoderrr_1_and, decoderrr_1_sub, decoderrr_1_or, decoderrr_1_ori, jal);

  // Notes on the sheet:
  //   无符号扩展
  //   mem_write
  //   beq
  //   memtoReg
  //   bne
endmodule

module uplevel (
);

  wire ctl_unity_1_alu_src, ctl_unity_1_ext_u, ctl_unity_1_j, ctl_unity_1_mem_write, ctl_unity_1_memyoreg,
       ctl_unity_1_reg_dst, ctl_unity_1_reg_write, ctl_unity_1_s_i;
  wire [3:0] ctl_unity_1_out_15;
  wire [4:0] multiplexer_2_out;
  wire [31:0] adder_1_out, alu_1_result, bit_extender_1_out, bit_extender_2_out, bit_extender_3_out,
       main_1_reg1, main_1_reg2_2, multiplexer_1_out, multiplexer_3_out, multiplexer_4_out,
       multiplexer_5_out, multiplexer_6_out, ram_1_data, register_1_q, rom_1_data;

  Multiplexer #(.width(32)) multiplexer_1 (
    .in0(adder_1_out), .in1({adder_1_out[31:28], rom_1_data[25:0], 2'b00}), .out(multiplexer_1_out));  // open: sel, en
  Register #(.width(32)) register_1 (.D(multiplexer_1_out), .Q(register_1_q));  // open: en, clk, clr
  Adder #(.width(32)) adder_1 (.a(register_1_q), .b(32'h4), .out(adder_1_out));  // open: cin, cout
  ROM #(.addrWidth(10), .dataWidth(32)) rom_1 (.addr(register_1_q[11:2]), .data(rom_1_data));  // open: sel
  ctl_unity ctl_unity_1 (
    .o0_no5(rom_1_data[31:26]), .f0_nf5(rom_1_data[5:0]), .out_15(ctl_unity_1_out_15),
    .ext_u(ctl_unity_1_ext_u), .alu_src(ctl_unity_1_alu_src), .s_i(ctl_unity_1_s_i),
    .reg_dst(ctl_unity_1_reg_dst), .reg_write(ctl_unity_1_reg_write), .mem_write(ctl_unity_1_mem_write),
    .memyoReg(ctl_unity_1_memyoreg), .j(ctl_unity_1_j));  // open: beq, bne, jal, jr
  Adder adder_2 ();  // open: a, b, out, cin, cout
  assign bit_extender_1_out = {{16{rom_1_data[15]}}, rom_1_data[15:0]};  // Bit_Extender bit_extender_1
  assign bit_extender_2_out = {{16{1'b0}}, rom_1_data[15:0]};  // Bit_Extender bit_extender_2
  assign bit_extender_3_out = {{27{1'b0}}, rom_1_data[10:6]};  // Bit_Extender bit_extender_3
  Multiplexer #(.width(5)) multiplexer_2 (
    .in0(rom_1_data[20:16]), .in1(rom_1_data[15:11]), .out(multiplexer_2_out), .sel(ctl_unity_1_reg_dst));  // open: en
  Multiplexer #(.width(32)) multiplexer_3 (
    .in0(bit_extender_1_out), .in1(bit_extender_2_out), .out(multiplexer_3_out), .sel(ctl_unity_1_ext_u));  // open: en
  Multiplexer #(.width(32)) multiplexer_4 (
    .in0(multiplexer_3_out), .in1(bit_extender_3_out), .out(multiplexer_4_out), .sel(ctl_unity_1_s_i));  // open: en
  \CS1409_U201414803_许荣仁_regfile_main  main_1 (
    .Reg1_num(rom_1_data[25:21]), .Reg2(rom_1_data[20:16]), .Write_Reg_num(multiplexer_2_out),
    .Din(multiplexer_6_out), .Write_Enable(ctl_unity_1_reg_write), .Reg1(main_1_reg1), .Reg2_2(main_1_reg2_2));  // open: Clock, s0_Value, s1_Value, s2_Value, ra_Value
  Multiplexer #(.width(32)) multiplexer_5 (
    .in0(main_1_reg2_2), .in1(multiplexer_4_out), .out(multiplexer_5_out), .sel(ctl_unity_1_alu_src));  // open: en
  ALU alu_1 (
    .AluOP(ctl_unity_1_out_15), .X(main_1_reg1), .Result(alu_1_result), .Y(multiplexer_5_out));  // open: Equal, Signed_Overflow, Result_2, UnSigned_Overflow
  RAM #(.addrWidth(10), .dataWidth(32), .bus("separate")) ram_1 (
    .addr(alu_1_result[9:0]), .din(main_1_reg2_2), .data(ram_1_data), .str(ctl_unity_1_mem_write));  // open: sel, clk, ld, clr
  Multiplexer #(.width(32)) multiplexer_6 (
    .in0(alu_1_result), .in1(ram_1_data), .out(multiplexer_6_out), .sel(ctl_unity_1_memyoreg));  // open: en
endmodule
